// Logisim project MasterLock.circ as structural Verilog: 1 circuit, main circuit main
// Reset
module main (
  input  [5:0] Key_A,
  input  [5:0] Key_B,
  input  Touch,
  input  AC,
  input  Pass_0,
  input  [5:0] Key_C,
  input  Lock,
  output o_p,
  output L,
  output Alarm
);

  wire and_1_out, and_2_out, and_3_out, and_4_out, and_5_out, and_6_out, and_7_out, and_8_out, and_9_out,
       and_10_out, and_11_out, and_12_out, CLK_out, comparator_1_eq, comparator_2_eq, comparator_3_eq,
       comparator_4_eq, not_1_out, not_2_out, not_3_out, not_4_out, or_1_out, or_2_out, or_3_out, or_4_out,
       or_5_out, or_6_out, or_7_out, or_8_out, S1_qn, Y0_q, Y0_qn, Y1_q, Y1_qn;
  wire [1:0] S0_q;
  wire [2:0] counter_1_q;
  wire [5:0] Counter_2_q, demultiplexer_1_out0, demultiplexer_1_out1, demultiplexer_1_out2;

  not not_1 (not_1_out, AC);
  and and_1 (and_1_out, not_1_out, S1_qn);
  and and_2 (and_2_out, S0_q[0], not_1_out);
  and and_3 (and_3_out, and_1_out, Pass_0);
  not not_2 (not_2_out, comparator_1_eq);
  Clock CLK (.out(CLK_out));
  or or_1 (or_1_out, and_2_out, and_3_out);
  and and_4 (and_4_out, not_2_out, Pass_0);
  D_Flip_Flop #(.trigger("falling")) S0 (
    .clk(CLK_out), .D(or_1_out), .Q(S0_q[0]), .en(1'b1), .reset(or_4_out));  // open: Qn, preset
  Counter #(.width(3), .max('h7)) counter_1 (
    .Q(counter_1_q), .clk(and_4_out), .clr(AC));  // open: load, D, count, carry
  and and_5 (and_5_out, AC, or_2_out);
  or or_2 (or_2_out, S0_q[0], S0_q[1]);
  Comparator #(.width(3)) comparator_1 (.a(3'b100), .b(counter_1_q), .eq(comparator_1_eq));  // open: gt, lt
  Counter #(.width(6), .max('h27)) Counter_2 (
    .load(AC), .count(1'b1), .Q(Counter_2_q), .clk(CLK_out), .clr(or_4_out));  // open: D, carry
  D_Flip_Flop #(.trigger("falling")) S1 (
    .clk(CLK_out), .D(and_5_out), .Q(S0_q[1]), .Qn(S1_qn), .en(1'b1), .reset(or_4_out));  // open: preset
  or or_3 (or_3_out, comparator_1_eq, Lock);
  Demultiplexer #(.select(2), .width(6)) demultiplexer_1 (
    .out0(demultiplexer_1_out0), .out1(demultiplexer_1_out1), .out2(demultiplexer_1_out2), .in(Counter_2_q),
    .sel(S0_q));  // open: out3, en
  or or_4 (or_4_out, Alarm, or_3_out);
  Comparator #(.width(6), .mode("unsigned")) comparator_2 (
    .a(demultiplexer_1_out0), .b(Key_A), .eq(comparator_2_eq));  // open: gt, lt
  Comparator #(.width(6), .mode("unsigned")) comparator_3 (
    .a(demultiplexer_1_out1), .b(Key_B), .eq(comparator_3_eq));  // open: gt, lt
  Comparator #(.width(6), .mode("unsigned")) comparator_4 (
    .a(demultiplexer_1_out2), .b(Key_C), .eq(comparator_4_eq));  // open: gt, lt
  and and_6 (and_6_out, AC, comparator_2_eq);
  and and_7 (and_7_out, not_1_out, comparator_3_eq);
  and and_8 (and_8_out, comparator_4_eq, AC);
  and and_9 (and_9_out, and_7_out, Pass_0);
  or or_5 (or_5_out, and_8_out, Y0_q, Y1_qn);
  not not_3 (not_3_out, and_9_out);
  or or_6 (or_6_out, not_3_out, Y0_qn, Y1_q);
  or or_7 (or_7_out, Y0_q, and_6_out, Y1_q);
  D_Flip_Flop #(.trigger("falling")) Y0 (
    .clk(CLK_out), .D(and_10_out), .Q(Y0_q), .Qn(Y0_qn), .en(1'b1), .reset(or_4_out));  // open: preset
  and and_10 (and_10_out, or_7_out, or_6_out, or_5_out);
  and and_11 (and_11_out, and_9_out, Y0_q);
  or or_8 (or_8_out, and_11_out, Y1_q);
  D_Flip_Flop #(.trigger("falling")) Y1 (
    .clk(CLK_out), .D(or_8_out), .Q(Y1_q), .Qn(Y1_qn), .en(1'b1), .reset(or_4_out));  // open: preset
  and and_12 (and_12_out, Touch, L);
  not not_4 (not_4_out, and_8_out);
  and and_13 (L, Y0_q, Y1_q);
  and and_14 (o_p, and_12_out, and_8_out);
  and and_15 (Alarm, not_4_out, Touch);
endmodule
